# Fritzing sketch VacHoseSwitchingBox_PCB (saved by Fritzing 0.9.4)
circuit board: 7cm x 7cm

parts:
  Nano = Arduino Nano (Rev3.0) (ICSP)
  Box_Cable = female alternating pin header, 8 pins [form="♀ (female)"]
  POS_1 = LED - 5mm [color="Yellow (595nm)" package="5 mm [THT]"]
  POS_2 = LED - 5mm [color="Yellow (595nm)" package="5 mm [THT]"]
  POS_3 = LED - 5mm [color="Yellow (595nm)" package="5 mm [THT]"]
  GND_12V = male alternating pin header, 2 pins [form="♂ (male)"]
  CHANGE_POSITION = Pushbutton [package="[THT]"]
  R1 = Resistor [tolerance=±5% resistance=330 package=THT]
  R2 = Resistor [tolerance=±5% resistance=330 package=THT]
  R3 = Resistor [tolerance=±5% resistance=330 package=THT]
  Q1 = NPN-Transistor [part_number=BC337 package="TO92 [THT]"]
  R4 = Resistor [tolerance=±5% resistance=1k package=THT]
  IR_Receiver = TSOP4838 [package=THT]
  R5 = Resistor [tolerance=±5% resistance=330 package=THT]
  IR_emitter = male alternating pin header, 2 pins [form="♂ (male)"]
  RESET = Pushbutton [package="[THT]"]

nets:
  N1: Nano.RESET, RESET.Pin_1, RESET.Pin_2
  GND: Nano.GND, Box_Cable.pin3, POS_1.cathode, POS_2.cathode, POS_3.cathode, GND_12V.pin2, CHANGE_POSITION.Pin_1, CHANGE_POSITION.Pin_2, Q1.E, IR_Receiver.GND, IR_emitter.pin2, RESET.Pin_3, RESET.Pin_4
  N2: Nano.D2, Box_Cable.pin7
  N3: Nano.D3, Box_Cable.pin5
  N4: Nano.D4, R5.Pin_0
  N5: Nano.D5, IR_Receiver.Out
  N6: Nano.D6, R1.Pin_0
  N7: Nano.D7, R2.Pin_0
  N8: Nano.D8, R3.Pin_0
  N9: Nano.D9, R4.Pin_0
  N10: Nano.D10, CHANGE_POSITION.Pin_3, CHANGE_POSITION.Pin_4
  N11: Nano.VIN, Box_Cable.pin1, GND_12V.pin1
  5V: Nano.5V, Box_Cable.pin4, IR_Receiver.Vcc
  N12: Box_Cable.pin2, Q1.C
  N13: POS_1.anode, R1.Pin_1
  N14: POS_2.anode, R2.Pin_1
  N15: POS_3.anode, R3.Pin_1
  N16: Q1.B, R4.Pin_1
  N17: R5.Pin_1, IR_emitter.pin1

notes:
  +
  -
  Violet       Moteur +
  Blanc       Moteur -
  Transp.     Effet Hall
  Gris       Encodeur B
  Jaune        Encoder A
  Bleu          VCC
  Marron          GND
  Orange       NC

custom parts:
  TSOP4838: The TSOP3848 are miniaturized receivers for infrared remote control systems. A PIN diode and a preamplifier are assembled on a lead frame, the epoxy package acts as an IR filter. The demodulated output signal can be directly decoded by a microprocessor. The TSOP4838 is compatible with all common IR remote control data formats.
